# Fritzing sketch placa_chassi (saved by Fritzing 0.9.3b)
circuit board: 14.4792cm x 9.2498cm

parts:
  US1 = hc-sr04
  US2 = hc-sr04
  US3 = hc-sr04
  US4 = hc-sr04
  US5 = hc-sr04
  US6 = hc-sr04
  US7 = hc-sr04
  US8 = hc-sr04
  J1 = female pin header, 12 pins [form="♀ (female)"]
  J3 = Power Jack [package=power_jack_pth]
  U1 = Voltage Regulator - 5V [package="TO220 [THT]"]
  J4 = female pin header, 2 pins [form="♀ (female)"]
  J5 = female pin header, 2 pins [form="♀ (female)"]
  J6 = female pin header, 2 pins [form="♀ (female)"]
  J7 = female pin header, 2 pins [form="♀ (female)"]
  J8 = female pin header, 2 pins [form="♀ (female)"]
  R1 = Resistor [tolerance=±5% resistance=220 package=THT]
  R2 = Resistor [tolerance=±5% resistance=220 package=THT]
  R3 = Resistor [tolerance=±5% resistance=220 package=THT]
  R4 = Resistor [tolerance=±5% resistance=220 package=THT]
  R5 = Resistor [tolerance=±5% resistance=220 package=THT]
  J9 = female pin header, 13 pins [form="♀ (female)"]
  J11 = female pin header, 6 pins [form="♀ (female)"]
  J14 = double row female pin header, 34 pins [form="♀ (female)"]
  J15 = female pin header, 6 pins [form="♀ (female)"]
  J16 = female pin header, 6 pins [form="♀ (female)"]
  J17 = female pin header, 6 pins [form="♀ (female)"]

nets:
  N1: US1.VCC, J14.pin34
  N2: US1.Trig, J14.pin33
  N3: US1.Echo, US2.Echo, US3.Echo, US4.Echo, US5.Echo, US6.Echo, US7.Echo, US8.Echo, U1.output_voltage, J4.pin1, J5.pin1, J6.pin1, J7.pin1, J8.pin1, J9.pin11, J11.pin4, J15.pin4, J16.pin4, J17.pin4
  GND: US1.GND, US2.GND, US3.GND, US4.GND, US5.GND, US6.GND, US7.GND, US8.GND, J1.pin7, J1.pin8, J3.GND, U1.GND, R1.Pin_1, R2.Pin_1, R3.Pin_1, R4.Pin_1, R5.Pin_1, J9.pin13, J11.pin3, J14.pin5, J15.pin3, J16.pin3, J17.pin3
  N4: US2.VCC, J14.pin32
  N5: US2.Trig, J14.pin31
  N6: US3.VCC, J14.pin30
  N7: US3.Trig, J14.pin29
  N8: US4.VCC, J14.pin28
  N9: US4.Trig, J14.pin27
  N10: US5.VCC, J14.pin26
  N11: US5.Trig, J14.pin25
  N12: US6.VCC, J14.pin24
  N13: US6.Trig, J14.pin23
  N14: US7.VCC, J14.pin22
  N15: US7.Trig, J14.pin21
  N16: US8.VCC, J14.pin20
  N17: US8.Trig, J14.pin19
  N18: J1.pin1, J1.pin2
  N19: J1.pin3, J1.pin4
  N20: J1.pin5, J1.pin6, J3.PWR, U1.input_voltage
  N21: J1.pin9, J1.pin10
  N22: J1.pin11, J1.pin12
  N23: J4.pin2, R1.Pin_0, J14.pin17
  N24: J5.pin2, R4.Pin_0, J14.pin15
  N25: J6.pin2, R3.Pin_0, J14.pin16
  N26: J7.pin2, R2.Pin_0, J14.pin18
  N27: J8.pin2, R5.Pin_0, J14.pin14
  N28: J9.pin2, J14.pin13
  N29: J9.pin3, J14.pin12
  N30: J9.pin4, J14.pin11
  N31: J9.pin7, J14.pin10
  N32: J9.pin8, J14.pin9
  N33: J9.pin9, J14.pin8
  N34: J11.pin1, J17.pin1
  N35: J11.pin2, J17.pin2
  N36: J11.pin5, J14.pin3
  N37: J11.pin6, J14.pin4
  N38: J14.pin1, J15.pin6
  N39: J14.pin2, J15.pin5
  N40: J15.pin1, J16.pin1
  N41: J15.pin2, J16.pin2
